// Digital circuit cpu.dig as structural Verilog
module cpu (
);

  wire [1:0] regfile_1_p1;
  wire [7:0] ALU_s, regfile_1_p2, regfile_1_p3;

  segfile segfile_1 ();  // open: in, seg_sel, wr_sel, wr_en, clk, seg
  // regfile regfile_1: pin names not known; wires that end beside it: regfile_1_p1, regfile_1_p2, regfile_1_p3
  Add #(.Bits(8)) ALU (.a(regfile_1_p2), .b(regfile_1_p3), .s(ALU_s));  // open: c_i, c_o
  RAMAsync ramasync_1 (.A(regfile_1_p1), .D(ALU_s[0]));  // open: we, Q
  // Pins of 1 and 8 bits meet at ALU_s
endmodule
